// Logisim project ADD.circ as structural Verilog: 1 circuit, main circuit main
module main (
  input  A0,
  input  B0,
  input  Cin,
  input  A1,
  input  B1,
  input  A2,
  input  B2,
  input  A3,
  input  B3,
  input  A4,
  input  B4,
  input  A2_2,
  input  B2_2,
  input  A2_3,
  input  B2_3,
  input  A2_4,
  input  B2_4,
  input  A2_5,
  input  B2_5,
  input  A2_6,
  input  B2_6,
  input  A2_7,
  input  B2_7,
  input  A2_8,
  input  B2_8,
  input  A2_9,
  input  B2_9,
  input  A2_10,
  input  B2_10,
  input  A2_11,
  input  B2_11,
  input  A2_12,
  input  B2_12,
  output D0,
  output D1,
  output D2,
  output D3,
  output D2_2,
  output D2_3,
  output D2_4,
  output D2_5,
  output D2_6,
  output D2_7,
  output D2_8,
  output D2_9,
  output D2_10,
  output D2_11,
  output D2_12,
  output D2_13
);

  wire and_1_out, and_2_out, and_3_out, and_4_out, and_5_out, and_6_out, and_7_out, and_8_out, and_9_out,
       and_10_out, and_11_out, and_12_out, and_13_out, and_14_out, and_15_out, and_16_out, and_17_out,
       and_18_out, and_19_out, and_20_out, and_21_out, and_22_out, and_23_out, and_24_out, and_25_out,
       and_26_out, and_27_out, and_28_out, and_29_out, and_30_out, and_31_out, and_32_out, and_33_out,
       and_34_out, and_35_out, and_36_out, and_37_out, and_38_out, and_39_out, and_40_out, and_41_out,
       and_42_out, and_43_out, and_44_out, and_45_out, and_46_out, and_47_out, and_48_out, or_1_out,
       or_2_out, or_3_out, or_4_out, or_5_out, or_6_out, or_7_out, or_8_out, or_9_out, or_10_out, or_11_out,
       or_12_out, or_13_out, or_14_out, or_15_out, or_16_out;

  and and_1 (and_1_out, A0, B0);
  and and_2 (and_2_out, B0, Cin);
  and and_3 (and_3_out, A0, Cin);
  and and_4 (and_4_out, A1, B1);
  and and_5 (and_5_out, B1, or_1_out);
  and and_6 (and_6_out, or_1_out, A1);
  and and_7 (and_7_out, A2, B2);
  and and_8 (and_8_out, B2, or_2_out);
  and and_9 (and_9_out, or_2_out, A2);
  and and_10 (and_10_out, A3, B3);
  and and_11 (and_11_out, B3, or_3_out);
  and and_12 (and_12_out, or_3_out, A3);
  and and_13 (and_13_out, A4, B4);
  and and_14 (and_14_out, B4, or_4_out);
  and and_15 (and_15_out, or_4_out, A4);
  and and_16 (and_16_out, A2_2, B2_2);
  and and_17 (and_17_out, B2_2, or_5_out);
  and and_18 (and_18_out, or_5_out, A2_2);
  and and_19 (and_19_out, A2_3, B2_3);
  and and_20 (and_20_out, B2_3, or_6_out);
  and and_21 (and_21_out, or_6_out, A2_3);
  and and_22 (and_22_out, A2_4, B2_4);
  and and_23 (and_23_out, B2_4, or_7_out);
  and and_24 (and_24_out, or_7_out, A2_4);
  and and_25 (and_25_out, A2_5, B2_5);
  and and_26 (and_26_out, B2_5, or_8_out);
  and and_27 (and_27_out, or_8_out, A2_5);
  and and_28 (and_28_out, A2_6, B2_6);
  and and_29 (and_29_out, B2_6, or_9_out);
  and and_30 (and_30_out, or_9_out, A2_6);
  and and_31 (and_31_out, A2_7, B2_7);
  and and_32 (and_32_out, B2_7, or_10_out);
  and and_33 (and_33_out, or_10_out, A2_7);
  and and_34 (and_34_out, A2_8, B2_8);
  and and_35 (and_35_out, B2_8, or_11_out);
  and and_36 (and_36_out, or_11_out, A2_8);
  and and_37 (and_37_out, A2_9, B2_9);
  and and_38 (and_38_out, B2_9, or_12_out);
  and and_39 (and_39_out, or_12_out, A2_9);
  and and_40 (and_40_out, A2_10, B2_10);
  and and_41 (and_41_out, B2_10, or_13_out);
  and and_42 (and_42_out, or_13_out, A2_10);
  and and_43 (and_43_out, A2_11, B2_11);
  and and_44 (and_44_out, B2_11, or_14_out);
  and and_45 (and_45_out, or_14_out, A2_11);
  and and_46 (and_46_out, A2_12, B2_12);
  and and_47 (and_47_out, B2_12, or_15_out);
  and and_48 (and_48_out, or_15_out, A2_12);
  or or_1 (or_1_out, and_1_out, and_2_out, and_3_out);
  or or_2 (or_2_out, and_4_out, and_5_out, and_6_out);
  or or_3 (or_3_out, and_7_out, and_8_out, and_9_out);
  or or_4 (or_4_out, and_10_out, and_11_out, and_12_out);
  or or_5 (or_5_out, and_13_out, and_14_out, and_15_out);
  or or_6 (or_6_out, and_16_out, and_17_out, and_18_out);
  or or_7 (or_7_out, and_19_out, and_20_out, and_21_out);
  or or_8 (or_8_out, and_22_out, and_23_out, and_24_out);
  or or_9 (or_9_out, and_25_out, and_26_out, and_27_out);
  or or_10 (or_10_out, and_28_out, and_29_out, and_30_out);
  or or_11 (or_11_out, and_31_out, and_32_out, and_33_out);
  or or_12 (or_12_out, and_34_out, and_35_out, and_36_out);
  or or_13 (or_13_out, and_37_out, and_38_out, and_39_out);
  or or_14 (or_14_out, and_40_out, and_41_out, and_42_out);
  or or_15 (or_15_out, and_43_out, and_44_out, and_45_out);
  or or_16 (or_16_out, and_46_out, and_47_out, and_48_out);
  ExactlyOne xor_1 (.out(D0), .in0(A0), .in1(B0), .in2(or_1_out));
  ExactlyOne xor_2 (.out(D1), .in0(A1), .in1(B1), .in2(or_2_out));
  ExactlyOne xor_3 (.out(D2), .in0(A2), .in1(B2), .in2(or_3_out));
  ExactlyOne xor_4 (.out(D3), .in0(A3), .in1(B3), .in2(or_4_out));
  ExactlyOne xor_5 (.out(D2_2), .in0(A4), .in1(B4), .in2(or_5_out));
  ExactlyOne xor_6 (.out(D2_3), .in0(A2_2), .in1(B2_2), .in2(or_6_out));
  ExactlyOne xor_7 (.out(D2_4), .in0(A2_3), .in1(B2_3), .in2(or_7_out));
  ExactlyOne xor_8 (.out(D2_5), .in0(A2_4), .in1(B2_4), .in2(or_8_out));
  ExactlyOne xor_9 (.out(D2_6), .in0(A2_5), .in1(B2_5), .in2(or_9_out));
  ExactlyOne xor_10 (.out(D2_7), .in0(A2_6), .in1(B2_6), .in2(or_10_out));
  ExactlyOne xor_11 (.out(D2_8), .in0(A2_7), .in1(B2_7), .in2(or_11_out));
  ExactlyOne xor_12 (.out(D2_9), .in0(A2_8), .in1(B2_8), .in2(or_12_out));
  ExactlyOne xor_13 (.out(D2_10), .in0(A2_9), .in1(B2_9), .in2(or_13_out));
  ExactlyOne xor_14 (.out(D2_11), .in0(A2_10), .in1(B2_10), .in2(or_14_out));
  ExactlyOne xor_15 (.out(D2_12), .in0(A2_11), .in1(B2_11), .in2(or_15_out));
  ExactlyOne xor_16 (.out(D2_13), .in0(A2_12), .in1(B2_12), .in2(or_16_out));
endmodule
