// Logisim project Input.circ as structural Verilog: 5 circuits, main circuit main
module main (
  input  in_1,
  input  in_2,
  input  [15:0] Rs_Value,
  input  [15:0] Rt_Value,
  input  [3:0] Rs,
  input  [3:0] Rt,
  input  [3:0] Rd,
  input  in_8,
  input  [3:0] OPCODE,
  input  in_10
);

  wire clock_1_out, decoder_1_out0, decoder_1_out1, decoder_1_out2, decoder_1_out3, decoder_1_out4,
       decoder_1_out5, decoder_1_out6, decoder_1_out7, decoder_1_out8, decoder_1_out9, decoder_1_out10,
       decoder_1_out11;
  wire [1:0] counter_1_q;
  wire [3:0] multiplexer_1_out;
  wire [15:0] adder_1_out_4, adder_2_out_4, and_1_out, and_2_out, and_3_out, bit_extender_1_out,
       multiplexer_2_out, multiplexer_3_out, multiplexer_4_out, multiplexer_5_out, nor_1_out, not_1_out,
       or_1_out, or_2_out, s0_q, s1_q, s2_q, s3_q, s4_q, s5_q, subtractor_1_out_4, t0_q, t1_q, t2_q, t3_q,
       t4_q, zero_q;

  Counter #(.width(2), .max('h3)) counter_1 (.Q(counter_1_q), .clk(clock_1_out));  // open: load, D, count, carry, clr
  Clock clock_1 (.out(clock_1_out));
  Multiplexer #(.select(2), .width(4), .enable("false")) multiplexer_1 (
    .in0(Rs), .in1(Rt), .in2(Rd), .out(multiplexer_1_out), .sel(counter_1_q));  // open: in3
  Decoder #(.select(4), .enable("false")) decoder_1 (
    .out0(decoder_1_out0), .out1(decoder_1_out1), .out2(decoder_1_out2), .out3(decoder_1_out3),
    .out4(decoder_1_out4), .out5(decoder_1_out5), .out6(decoder_1_out6), .out7(decoder_1_out7),
    .out8(decoder_1_out8), .out9(decoder_1_out9), .out10(decoder_1_out10), .out11(decoder_1_out11),
    .sel(multiplexer_1_out));  // open: out12, out13, out14, out15
  Multiplexer #(.select(2), .width(16), .enable("false")) multiplexer_2 (
    .in0(Rs_Value), .in1(Rt_Value), .in2(multiplexer_5_out), .out(multiplexer_2_out), .sel(counter_1_q));  // open: in3
  Register #(.width(16)) zero (.en(decoder_1_out0), .Q(zero_q), .clk(clock_1_out), .clr(in_10));  // open: D
  Register #(.width(16)) s0 (.D(multiplexer_2_out), .en(decoder_1_out1), .Q(s0_q), .clk(clock_1_out), .clr(in_10));
  Register #(.width(16)) s1 (.D(multiplexer_2_out), .en(decoder_1_out2), .Q(s1_q), .clk(clock_1_out), .clr(in_10));
  Register #(.width(16)) s2 (.D(multiplexer_2_out), .en(decoder_1_out3), .Q(s2_q), .clk(clock_1_out), .clr(in_10));
  Register #(.width(16)) s3 (.D(multiplexer_2_out), .en(decoder_1_out4), .Q(s3_q), .clk(clock_1_out), .clr(in_10));
  Register #(.width(16)) s4 (.D(multiplexer_2_out), .en(decoder_1_out5), .Q(s4_q), .clk(clock_1_out), .clr(in_10));
  Register #(.width(16)) s5 (.D(multiplexer_2_out), .en(decoder_1_out6), .Q(s5_q), .clk(clock_1_out), .clr(in_10));
  Register #(.width(16)) t0 (.D(multiplexer_2_out), .en(decoder_1_out7), .Q(t0_q), .clk(clock_1_out), .clr(in_10));
  Register #(.width(16)) t1 (.D(multiplexer_2_out), .en(decoder_1_out8), .Q(t1_q), .clk(clock_1_out), .clr(in_10));
  Register #(.width(16)) t2 (.D(multiplexer_2_out), .en(decoder_1_out9), .Q(t2_q), .clk(clock_1_out), .clr(in_10));
  Register #(.width(16)) t3 (.D(multiplexer_2_out), .en(decoder_1_out10), .Q(t3_q), .clk(clock_1_out), .clr(in_10));
  Register #(.width(16)) t4 (.D(multiplexer_2_out), .en(decoder_1_out11), .Q(t4_q), .clk(clock_1_out), .clr(in_10));
  assign bit_extender_1_out = {{12{1'b0}}, Rt};  // Bit_Extender bit_extender_1
  Multiplexer #(.select(4), .width(16), .enable("false")) multiplexer_3 (
    .in0(zero_q), .in1(s0_q), .in2(s1_q), .in3(s2_q), .in4(s3_q), .in5(s4_q), .in6(s5_q), .in7(t0_q),
    .in8(t1_q), .in9(t2_q), .in10(t3_q), .in11(t4_q), .out(multiplexer_3_out), .sel(Rs));  // open: in12, in13, in14, in15
  Multiplexer #(.select(4), .width(16), .enable("false")) multiplexer_4 (
    .in0(zero_q), .in1(s0_q), .in2(s1_q), .in3(s2_q), .in4(s3_q), .in5(s4_q), .in6(s5_q), .in7(t0_q),
    .in8(t1_q), .in9(t2_q), .in10(t3_q), .in11(t4_q), .out(multiplexer_4_out), .sel(Rt));  // open: in12, in13, in14, in15
  assign not_1_out = ~multiplexer_3_out;  // NOT_Gate not_1, 16 bits wide
  Adder adder_1 (.Cin(in_1), .in_2(multiplexer_3_out), .in_3(multiplexer_4_out), .out_4(adder_1_out_4));
  Subtractor subtractor_1 (.in_1(multiplexer_3_out), .in_2(in_2), .in_3(multiplexer_4_out), .out_4(subtractor_1_out_4));
  assign and_1_out = multiplexer_3_out & multiplexer_4_out;  // AND_Gate and_1, 16 bits wide
  assign or_1_out = multiplexer_3_out | multiplexer_4_out;  // OR_Gate or_1, 16 bits wide
  assign and_2_out = not_1_out & multiplexer_4_out;  // AND_Gate and_2, 16 bits wide
  assign and_3_out = multiplexer_3_out & bit_extender_1_out;  // AND_Gate and_3, 16 bits wide
  assign or_2_out = multiplexer_3_out | bit_extender_1_out;  // OR_Gate or_2, 16 bits wide
  Adder adder_2 (.Cin(in_8), .in_2(multiplexer_3_out), .in_3(bit_extender_1_out), .out_4(adder_2_out_4));
  assign nor_1_out = ~(multiplexer_3_out | multiplexer_4_out);  // NOR_Gate nor_1, 16 bits wide
  Multiplexer #(.select(4), .width(16), .enable("false")) multiplexer_5 (
    .in0(adder_1_out_4), .in1(subtractor_1_out_4), .in2(and_1_out), .in3(or_1_out), .in4(nor_1_out),
    .in7(and_2_out), .in8(and_3_out), .in9(or_2_out), .in10(adder_2_out_4), .out(multiplexer_5_out),
    .sel(OPCODE));  // open: in5, in6, in11, in12, in13, in14, in15
endmodule

module Adder (
  input  Cin,
  input  [15:0] in_2,
  input  [15:0] in_3,
  output [15:0] out_4
);

  wire and_1_out, and_2_out, and_3_out, and_4_out, and_5_out, and_6_out, and_7_out, and_8_out, and_9_out,
       and_10_out, and_11_out, and_12_out, and_13_out, and_14_out, and_15_out, and_16_out, and_17_out,
       and_18_out, and_19_out, and_20_out, and_21_out, and_22_out, and_23_out, and_24_out, and_25_out,
       and_26_out, and_27_out, and_28_out, and_29_out, and_30_out, and_31_out, and_32_out, and_33_out,
       and_34_out, and_35_out, and_36_out, and_37_out, and_38_out, and_39_out, and_40_out, and_41_out,
       and_42_out, and_43_out, and_44_out, and_45_out, and_46_out, and_47_out, and_48_out, or_1_out,
       or_2_out, or_3_out, or_4_out, or_5_out, or_6_out, or_7_out, or_8_out, or_9_out, or_10_out, or_11_out,
       or_12_out, or_13_out, or_14_out, or_15_out, or_16_out;

  and and_1 (and_1_out, in_2[0], in_3[0]);
  and and_2 (and_2_out, in_3[0], Cin);
  and and_3 (and_3_out, in_2[0], Cin);
  and and_4 (and_4_out, in_2[1], in_3[1]);
  and and_5 (and_5_out, in_3[1], or_1_out);
  and and_6 (and_6_out, or_1_out, in_2[1]);
  and and_7 (and_7_out, in_2[2], in_3[2]);
  and and_8 (and_8_out, in_3[2], or_2_out);
  and and_9 (and_9_out, or_2_out, in_2[2]);
  and and_10 (and_10_out, in_2[3], in_3[3]);
  and and_11 (and_11_out, in_3[3], or_3_out);
  and and_12 (and_12_out, or_3_out, in_2[3]);
  and and_13 (and_13_out, in_2[4], in_3[4]);
  and and_14 (and_14_out, in_3[4], or_4_out);
  and and_15 (and_15_out, or_4_out, in_2[4]);
  and and_16 (and_16_out, in_2[5], in_3[5]);
  and and_17 (and_17_out, in_3[5], or_5_out);
  and and_18 (and_18_out, or_5_out, in_2[5]);
  and and_19 (and_19_out, in_2[6], in_3[6]);
  and and_20 (and_20_out, in_3[6], or_6_out);
  and and_21 (and_21_out, or_6_out, in_2[6]);
  and and_22 (and_22_out, in_2[7], in_3[7]);
  and and_23 (and_23_out, in_3[7], or_7_out);
  and and_24 (and_24_out, or_7_out, in_2[7]);
  and and_25 (and_25_out, in_2[8], in_3[8]);
  and and_26 (and_26_out, in_3[8], or_8_out);
  and and_27 (and_27_out, or_8_out, in_2[8]);
  and and_28 (and_28_out, in_2[9], in_3[9]);
  and and_29 (and_29_out, in_3[9], or_9_out);
  and and_30 (and_30_out, or_9_out, in_2[9]);
  and and_31 (and_31_out, in_2[10], in_3[10]);
  and and_32 (and_32_out, in_3[10], or_10_out);
  and and_33 (and_33_out, or_10_out, in_2[10]);
  and and_34 (and_34_out, in_2[11], in_3[11]);
  and and_35 (and_35_out, in_3[11], or_11_out);
  and and_36 (and_36_out, or_11_out, in_2[11]);
  and and_37 (and_37_out, in_2[12], in_3[12]);
  and and_38 (and_38_out, in_3[12], or_12_out);
  and and_39 (and_39_out, or_12_out, in_2[12]);
  and and_40 (and_40_out, in_2[13], in_3[13]);
  and and_41 (and_41_out, in_3[13], or_13_out);
  and and_42 (and_42_out, or_13_out, in_2[13]);
  and and_43 (and_43_out, in_2[14], in_3[14]);
  and and_44 (and_44_out, in_3[14], or_14_out);
  and and_45 (and_45_out, or_14_out, in_2[14]);
  and and_46 (and_46_out, in_2[15], in_3[15]);
  and and_47 (and_47_out, in_3[15], or_15_out);
  and and_48 (and_48_out, or_15_out, in_2[15]);
  or or_1 (or_1_out, and_1_out, and_2_out, and_3_out);
  or or_2 (or_2_out, and_4_out, and_5_out, and_6_out);
  or or_3 (or_3_out, and_7_out, and_8_out, and_9_out);
  or or_4 (or_4_out, and_10_out, and_11_out, and_12_out);
  or or_5 (or_5_out, and_13_out, and_14_out, and_15_out);
  or or_6 (or_6_out, and_16_out, and_17_out, and_18_out);
  or or_7 (or_7_out, and_19_out, and_20_out, and_21_out);
  or or_8 (or_8_out, and_22_out, and_23_out, and_24_out);
  or or_9 (or_9_out, and_25_out, and_26_out, and_27_out);
  or or_10 (or_10_out, and_28_out, and_29_out, and_30_out);
  or or_11 (or_11_out, and_31_out, and_32_out, and_33_out);
  or or_12 (or_12_out, and_34_out, and_35_out, and_36_out);
  or or_13 (or_13_out, and_37_out, and_38_out, and_39_out);
  or or_14 (or_14_out, and_40_out, and_41_out, and_42_out);
  or or_15 (or_15_out, and_43_out, and_44_out, and_45_out);
  or or_16 (or_16_out, and_46_out, and_47_out, and_48_out);
  ExactlyOne xor_1 (.out(out_4[0]), .in0(in_2[0]), .in1(in_3[0]), .in2(or_1_out));
  ExactlyOne xor_2 (.out(out_4[1]), .in0(in_2[1]), .in1(in_3[1]), .in2(or_2_out));
  ExactlyOne xor_3 (.out(out_4[2]), .in0(in_2[2]), .in1(in_3[2]), .in2(or_3_out));
  ExactlyOne xor_4 (.out(out_4[3]), .in0(in_2[3]), .in1(in_3[3]), .in2(or_4_out));
  ExactlyOne xor_5 (.out(out_4[4]), .in0(in_2[4]), .in1(in_3[4]), .in2(or_5_out));
  ExactlyOne xor_6 (.out(out_4[5]), .in0(in_2[5]), .in1(in_3[5]), .in2(or_6_out));
  ExactlyOne xor_7 (.out(out_4[6]), .in0(in_2[6]), .in1(in_3[6]), .in2(or_7_out));
  ExactlyOne xor_8 (.out(out_4[7]), .in0(in_2[7]), .in1(in_3[7]), .in2(or_8_out));
  ExactlyOne xor_9 (.out(out_4[8]), .in0(in_2[8]), .in1(in_3[8]), .in2(or_9_out));
  ExactlyOne xor_10 (.out(out_4[9]), .in0(in_2[9]), .in1(in_3[9]), .in2(or_10_out));
  ExactlyOne xor_11 (.out(out_4[10]), .in0(in_2[10]), .in1(in_3[10]), .in2(or_11_out));
  ExactlyOne xor_12 (.out(out_4[11]), .in0(in_2[11]), .in1(in_3[11]), .in2(or_12_out));
  ExactlyOne xor_13 (.out(out_4[12]), .in0(in_2[12]), .in1(in_3[12]), .in2(or_13_out));
  ExactlyOne xor_14 (.out(out_4[13]), .in0(in_2[13]), .in1(in_3[13]), .in2(or_14_out));
  ExactlyOne xor_15 (.out(out_4[14]), .in0(in_2[14]), .in1(in_3[14]), .in2(or_15_out));
  ExactlyOne xor_16 (.out(out_4[15]), .in0(in_2[15]), .in1(in_3[15]), .in2(or_16_out));
endmodule

module Subtractor (
  input  [15:0] in_1,
  input  in_2,
  input  [15:0] in_3,
  output [15:0] out_4
);

  wire [15:0] adder_1_out_4, bit_extender_1_out, not_1_out;

  assign bit_extender_1_out = {{15{1'b0}}, in_2};  // Bit_Extender bit_extender_1
  assign not_1_out = ~in_3;  // NOT_Gate not_1, 16 bits wide
  Adder adder_1 (.in_2(bit_extender_1_out), .in_3(not_1_out), .out_4(adder_1_out_4));  // open: Cin
  Adder adder_2 (.in_2(in_1), .in_3(adder_1_out_4), .out_4(out_4));  // open: Cin
endmodule

module Sll (
  input  in_1,
  input  in_2,
  input  in_3,
  input  in_4,
  input  in_5,
  input  in_6,
  input  in_7,
  input  in_8,
  input  in_9,
  input  in_10,
  input  in_11,
  input  in_12,
  input  in_13,
  input  in_14,
  input  in_15,
  input  in_16,
  input  in_17,
  input  in_18,
  output out_19,
  output out_20,
  output out_21,
  output out_22,
  output out_23,
  output out_24,
  output out_25,
  output out_26,
  output out_27,
  output out_28,
  output out_29,
  output out_30,
  output out_31,
  output out_32,
  output out_33,
  output out_34
);

  wire clock_1_out, multiplexer_1_out, multiplexer_2_out, multiplexer_3_out, multiplexer_4_out,
       multiplexer_5_out, multiplexer_6_out, multiplexer_7_out, multiplexer_8_out, multiplexer_9_out,
       multiplexer_10_out, multiplexer_11_out, multiplexer_12_out, multiplexer_13_out, multiplexer_14_out,
       multiplexer_15_out, multiplexer_16_out;

  Clock clock_1 (.out(clock_1_out));
  Multiplexer #(.enable("false")) multiplexer_1 (.in0(in_7), .in1(out_23), .out(multiplexer_1_out), .sel(in_2));
  D_Flip_Flop d_ff_1 (.clk(clock_1_out), .D(multiplexer_1_out), .Q(out_19), .en(in_1));  // open: Qn, preset, reset
  D_Flip_Flop d_ff_2 (.clk(clock_1_out), .D(multiplexer_2_out), .Q(out_20), .en(in_1));  // open: Qn, preset, reset
  Multiplexer #(.enable("false")) multiplexer_2 (.in0(in_8), .in1(out_24), .out(multiplexer_2_out), .sel(in_2));
  D_Flip_Flop d_ff_3 (.clk(clock_1_out), .D(multiplexer_3_out), .Q(out_21), .en(in_1));  // open: Qn, preset, reset
  Multiplexer #(.enable("false")) multiplexer_3 (.in0(in_9), .in1(out_25), .out(multiplexer_3_out), .sel(in_2));
  D_Flip_Flop d_ff_4 (.clk(clock_1_out), .D(multiplexer_4_out), .Q(out_22), .en(in_1));  // open: Qn, preset, reset
  Multiplexer #(.enable("false")) multiplexer_4 (.in0(in_10), .in1(out_29), .out(multiplexer_4_out), .sel(in_2));
  D_Flip_Flop d_ff_5 (.clk(clock_1_out), .D(multiplexer_5_out), .Q(out_23), .en(in_1));  // open: Qn, preset, reset
  Multiplexer #(.enable("false")) multiplexer_5 (.in0(in_11), .in1(out_26), .out(multiplexer_5_out), .sel(in_2));
  D_Flip_Flop d_ff_6 (.clk(clock_1_out), .D(multiplexer_6_out), .Q(out_24), .en(in_1));  // open: Qn, preset, reset
  Multiplexer #(.enable("false")) multiplexer_6 (.in0(in_12), .in1(out_27), .out(multiplexer_6_out), .sel(in_2));
  D_Flip_Flop d_ff_7 (.clk(clock_1_out), .D(multiplexer_7_out), .Q(out_25), .en(in_1));  // open: Qn, preset, reset
  Multiplexer #(.enable("false")) multiplexer_7 (.in0(in_13), .in1(out_31), .out(multiplexer_7_out), .sel(in_2));
  D_Flip_Flop d_ff_8 (.clk(clock_1_out), .D(multiplexer_8_out), .Q(out_29), .en(in_1));  // open: Qn, preset, reset
  Multiplexer #(.enable("false")) multiplexer_8 (.in0(in_14), .in1(out_32), .out(multiplexer_8_out), .sel(in_2));
  D_Flip_Flop d_ff_9 (.clk(clock_1_out), .D(multiplexer_9_out), .Q(out_26), .en(in_1));  // open: Qn, preset, reset
  Multiplexer #(.enable("false")) multiplexer_9 (.in0(in_15), .in1(out_33), .out(multiplexer_9_out), .sel(in_2));
  D_Flip_Flop d_ff_10 (.clk(clock_1_out), .D(multiplexer_10_out), .Q(out_27), .en(in_1));  // open: Qn, preset, reset
  Multiplexer #(.enable("false")) multiplexer_10 (.in0(in_18), .in1(out_34), .out(multiplexer_10_out), .sel(in_2));
  D_Flip_Flop d_ff_11 (.clk(clock_1_out), .D(multiplexer_11_out), .Q(out_31), .en(in_1));  // open: Qn, preset, reset
  D_Flip_Flop d_ff_12 (.clk(clock_1_out), .D(multiplexer_12_out), .Q(out_32), .en(in_1));  // open: Qn, preset, reset
  Multiplexer #(.enable("false")) multiplexer_11 (.in0(in_3), .in1(out_30), .out(multiplexer_11_out), .sel(in_2));
  D_Flip_Flop d_ff_13 (.clk(clock_1_out), .D(multiplexer_13_out), .Q(out_33), .en(in_1));  // open: Qn, preset, reset
  Multiplexer #(.enable("false")) multiplexer_12 (.in0(in_16), .in1(out_28), .out(multiplexer_12_out), .sel(in_2));
  D_Flip_Flop d_ff_14 (.clk(clock_1_out), .D(multiplexer_14_out), .Q(out_34), .en(in_1));  // open: Qn, preset, reset
  Multiplexer #(.enable("false")) multiplexer_13 (.in0(in_17), .in1(out_19), .out(multiplexer_13_out), .sel(in_2));
  Multiplexer #(.enable("false")) multiplexer_14 (.in0(in_4), .in1(out_20), .out(multiplexer_14_out), .sel(in_2));
  D_Flip_Flop d_ff_15 (.clk(clock_1_out), .D(multiplexer_15_out), .Q(out_30), .en(in_1));  // open: Qn, preset, reset
  Multiplexer #(.enable("false")) multiplexer_15 (.in0(in_5), .in1(out_21), .out(multiplexer_15_out), .sel(in_2));
  D_Flip_Flop d_ff_16 (.clk(clock_1_out), .D(multiplexer_16_out), .Q(out_28), .en(in_1));  // open: Qn, preset, reset
  Multiplexer #(.enable("false")) multiplexer_16 (.in0(in_6), .in1(out_22), .out(multiplexer_16_out), .sel(in_2));
endmodule

module Srl (
  input  in_1,
  input  in_2,
  input  in_3,
  input  in_4,
  input  in_5,
  input  in_6,
  input  in_7,
  input  in_8,
  input  in_9,
  input  in_10,
  input  in_11,
  input  in_12,
  input  in_13,
  input  in_14,
  input  in_15,
  input  in_16,
  input  in_17,
  input  in_18,
  output out_19,
  output out_20,
  output out_21,
  output out_22,
  output out_23,
  output out_24,
  output out_25,
  output out_26,
  output out_27,
  output out_28,
  output out_29,
  output out_30,
  output out_31,
  output out_32,
  output out_33,
  output out_34
);

  wire clock_1_out, multiplexer_1_out, multiplexer_2_out, multiplexer_3_out, multiplexer_4_out,
       multiplexer_5_out, multiplexer_6_out, multiplexer_7_out, multiplexer_8_out, multiplexer_9_out,
       multiplexer_10_out, multiplexer_11_out, multiplexer_12_out, multiplexer_13_out, multiplexer_14_out,
       multiplexer_15_out, multiplexer_16_out;

  Clock clock_1 (.out(clock_1_out));
  Multiplexer #(.enable("false")) multiplexer_1 (.in0(in_7), .in1(out_33), .out(multiplexer_1_out), .sel(in_2));
  D_Flip_Flop d_ff_1 (.clk(clock_1_out), .D(multiplexer_1_out), .Q(out_19), .en(in_1));  // open: Qn, preset, reset
  D_Flip_Flop d_ff_2 (.clk(clock_1_out), .D(multiplexer_2_out), .Q(out_20), .en(in_1));  // open: Qn, preset, reset
  Multiplexer #(.enable("false")) multiplexer_2 (.in0(in_8), .in1(out_34), .out(multiplexer_2_out), .sel(in_2));
  D_Flip_Flop d_ff_3 (.clk(clock_1_out), .D(multiplexer_3_out), .Q(out_21), .en(in_1));  // open: Qn, preset, reset
  Multiplexer #(.enable("false")) multiplexer_3 (.in0(in_9), .in1(out_30), .out(multiplexer_3_out), .sel(in_2));
  D_Flip_Flop d_ff_4 (.clk(clock_1_out), .D(multiplexer_4_out), .Q(out_22), .en(in_1));  // open: Qn, preset, reset
  Multiplexer #(.enable("false")) multiplexer_4 (.in0(in_10), .in1(out_28), .out(multiplexer_4_out), .sel(in_2));
  D_Flip_Flop d_ff_5 (.clk(clock_1_out), .D(multiplexer_5_out), .Q(out_23), .en(in_1));  // open: Qn, preset, reset
  Multiplexer #(.enable("false")) multiplexer_5 (.in0(in_11), .in1(out_19), .out(multiplexer_5_out), .sel(in_2));
  D_Flip_Flop d_ff_6 (.clk(clock_1_out), .D(multiplexer_6_out), .Q(out_24), .en(in_1));  // open: Qn, preset, reset
  Multiplexer #(.enable("false")) multiplexer_6 (.in0(in_12), .in1(out_20), .out(multiplexer_6_out), .sel(in_2));
  D_Flip_Flop d_ff_7 (.clk(clock_1_out), .D(multiplexer_7_out), .Q(out_25), .en(in_1));  // open: Qn, preset, reset
  Multiplexer #(.enable("false")) multiplexer_7 (.in0(in_13), .in1(out_21), .out(multiplexer_7_out), .sel(in_2));
  D_Flip_Flop d_ff_8 (.clk(clock_1_out), .D(multiplexer_8_out), .Q(out_29), .en(in_1));  // open: Qn, preset, reset
  Multiplexer #(.enable("false")) multiplexer_8 (.in0(in_14), .in1(out_22), .out(multiplexer_8_out), .sel(in_2));
  D_Flip_Flop d_ff_9 (.clk(clock_1_out), .D(multiplexer_9_out), .Q(out_26), .en(in_1));  // open: Qn, preset, reset
  Multiplexer #(.enable("false")) multiplexer_9 (.in0(in_15), .in1(out_23), .out(multiplexer_9_out), .sel(in_2));
  D_Flip_Flop d_ff_10 (.clk(clock_1_out), .D(multiplexer_10_out), .Q(out_27), .en(in_1));  // open: Qn, preset, reset
  Multiplexer #(.enable("false")) multiplexer_10 (.in0(in_18), .in1(out_24), .out(multiplexer_10_out), .sel(in_2));
  D_Flip_Flop d_ff_11 (.clk(clock_1_out), .D(multiplexer_11_out), .Q(out_31), .en(in_1));  // open: Qn, preset, reset
  D_Flip_Flop d_ff_12 (.clk(clock_1_out), .D(multiplexer_12_out), .Q(out_32), .en(in_1));  // open: Qn, preset, reset
  Multiplexer #(.enable("false")) multiplexer_11 (.in0(in_3), .in1(out_25), .out(multiplexer_11_out), .sel(in_2));
  D_Flip_Flop d_ff_13 (.clk(clock_1_out), .D(multiplexer_13_out), .Q(out_33), .en(in_1));  // open: Qn, preset, reset
  Multiplexer #(.enable("false")) multiplexer_12 (.in0(in_16), .in1(out_29), .out(multiplexer_12_out), .sel(in_2));
  D_Flip_Flop d_ff_14 (.clk(clock_1_out), .D(multiplexer_14_out), .Q(out_34), .en(in_1));  // open: Qn, preset, reset
  Multiplexer #(.enable("false")) multiplexer_13 (.in0(in_17), .in1(out_26), .out(multiplexer_13_out), .sel(in_2));
  Multiplexer #(.enable("false")) multiplexer_14 (.in0(in_4), .in1(out_27), .out(multiplexer_14_out), .sel(in_2));
  D_Flip_Flop d_ff_15 (.clk(clock_1_out), .D(multiplexer_15_out), .Q(out_30), .en(in_1));  // open: Qn, preset, reset
  Multiplexer #(.enable("false")) multiplexer_15 (.in0(in_5), .in1(out_31), .out(multiplexer_15_out), .sel(in_2));
  D_Flip_Flop d_ff_16 (.clk(clock_1_out), .D(multiplexer_16_out), .Q(out_28), .en(in_1));  // open: Qn, preset, reset
  Multiplexer #(.enable("false")) multiplexer_16 (.in0(in_6), .in1(out_32), .out(multiplexer_16_out), .sel(in_2));
endmodule
