// Logisim project Project try(2).circ as structural Verilog: 2 circuits, main circuit main
module main (
  input  [1:0] in_1
);

  wire [1:0] adder_1_out, bit_extender_1_out;
  wire [3:0] rom_1_data;
  wire [15:0] rom_2_data;

  Bit_Extender #(.in_width(4), .out_width(2)) bit_extender_1 (.in(rom_1_data), .out(bit_extender_1_out));
  ROM #(.addrWidth(2), .dataWidth(4)) rom_1 (.addr(adder_1_out), .data(rom_1_data));  // open: sel
  Adder_part #(.width(2)) adder_1 (.a(in_1), .b(bit_extender_1_out), .out(adder_1_out));  // open: cin, cout
  ROM #(.addrWidth(4), .dataWidth(16)) rom_2 (.addr(rom_1_data), .data(rom_2_data));  // open: sel
endmodule

module Adder (
  input  Cin,
  input  [15:0] in_2,
  input  [15:0] in_3,
  output [15:0] out_4
);

  wire and_1_out, and_2_out, and_3_out, and_4_out, and_5_out, and_6_out, and_7_out, and_8_out, and_9_out,
       and_10_out, and_11_out, and_12_out, and_13_out, and_14_out, and_15_out, and_16_out, and_17_out,
       and_18_out, and_19_out, and_20_out, and_21_out, and_22_out, and_23_out, and_24_out, and_25_out,
       and_26_out, and_27_out, and_28_out, and_29_out, and_30_out, and_31_out, and_32_out, and_33_out,
       and_34_out, and_35_out, and_36_out, and_37_out, and_38_out, and_39_out, and_40_out, and_41_out,
       and_42_out, and_43_out, and_44_out, and_45_out, and_46_out, and_47_out, and_48_out, or_1_out,
       or_2_out, or_3_out, or_4_out, or_5_out, or_6_out, or_7_out, or_8_out, or_9_out, or_10_out, or_11_out,
       or_12_out, or_13_out, or_14_out, or_15_out, or_16_out;

  and and_1 (and_1_out, in_2[0], in_3[0]);
  and and_2 (and_2_out, in_3[0], Cin);
  and and_3 (and_3_out, in_2[0], Cin);
  and and_4 (and_4_out, in_2[1], in_3[1]);
  and and_5 (and_5_out, in_3[1], or_1_out);
  and and_6 (and_6_out, or_1_out, in_2[1]);
  and and_7 (and_7_out, in_2[2], in_3[2]);
  and and_8 (and_8_out, in_3[2], or_2_out);
  and and_9 (and_9_out, or_2_out, in_2[2]);
  and and_10 (and_10_out, in_2[3], in_3[3]);
  and and_11 (and_11_out, in_3[3], or_3_out);
  and and_12 (and_12_out, or_3_out, in_2[3]);
  and and_13 (and_13_out, in_2[4], in_3[4]);
  and and_14 (and_14_out, in_3[4], or_4_out);
  and and_15 (and_15_out, or_4_out, in_2[4]);
  and and_16 (and_16_out, in_2[5], in_3[5]);
  and and_17 (and_17_out, in_3[5], or_5_out);
  and and_18 (and_18_out, or_5_out, in_2[5]);
  and and_19 (and_19_out, in_2[6], in_3[6]);
  and and_20 (and_20_out, in_3[6], or_6_out);
  and and_21 (and_21_out, or_6_out, in_2[6]);
  and and_22 (and_22_out, in_2[7], in_3[7]);
  and and_23 (and_23_out, in_3[7], or_7_out);
  and and_24 (and_24_out, or_7_out, in_2[7]);
  and and_25 (and_25_out, in_2[8], in_3[8]);
  and and_26 (and_26_out, in_3[8], or_8_out);
  and and_27 (and_27_out, or_8_out, in_2[8]);
  and and_28 (and_28_out, in_2[9], in_3[9]);
  and and_29 (and_29_out, in_3[9], or_9_out);
  and and_30 (and_30_out, or_9_out, in_2[9]);
  and and_31 (and_31_out, in_2[10], in_3[10]);
  and and_32 (and_32_out, in_3[10], or_10_out);
  and and_33 (and_33_out, or_10_out, in_2[10]);
  and and_34 (and_34_out, in_2[11], in_3[11]);
  and and_35 (and_35_out, in_3[11], or_11_out);
  and and_36 (and_36_out, or_11_out, in_2[11]);
  and and_37 (and_37_out, in_2[12], in_3[12]);
  and and_38 (and_38_out, in_3[12], or_12_out);
  and and_39 (and_39_out, or_12_out, in_2[12]);
  and and_40 (and_40_out, in_2[13], in_3[13]);
  and and_41 (and_41_out, in_3[13], or_13_out);
  and and_42 (and_42_out, or_13_out, in_2[13]);
  and and_43 (and_43_out, in_2[14], in_3[14]);
  and and_44 (and_44_out, in_3[14], or_14_out);
  and and_45 (and_45_out, or_14_out, in_2[14]);
  and and_46 (and_46_out, in_2[15], in_3[15]);
  and and_47 (and_47_out, in_3[15], or_15_out);
  and and_48 (and_48_out, or_15_out, in_2[15]);
  or or_1 (or_1_out, and_1_out, and_2_out, and_3_out);
  or or_2 (or_2_out, and_4_out, and_5_out, and_6_out);
  or or_3 (or_3_out, and_7_out, and_8_out, and_9_out);
  or or_4 (or_4_out, and_10_out, and_11_out, and_12_out);
  or or_5 (or_5_out, and_13_out, and_14_out, and_15_out);
  or or_6 (or_6_out, and_16_out, and_17_out, and_18_out);
  or or_7 (or_7_out, and_19_out, and_20_out, and_21_out);
  or or_8 (or_8_out, and_22_out, and_23_out, and_24_out);
  or or_9 (or_9_out, and_25_out, and_26_out, and_27_out);
  or or_10 (or_10_out, and_28_out, and_29_out, and_30_out);
  or or_11 (or_11_out, and_31_out, and_32_out, and_33_out);
  or or_12 (or_12_out, and_34_out, and_35_out, and_36_out);
  or or_13 (or_13_out, and_37_out, and_38_out, and_39_out);
  or or_14 (or_14_out, and_40_out, and_41_out, and_42_out);
  or or_15 (or_15_out, and_43_out, and_44_out, and_45_out);
  or or_16 (or_16_out, and_46_out, and_47_out, and_48_out);
  ExactlyOne xor_1 (.out(out_4[0]), .in0(in_2[0]), .in1(in_3[0]), .in2(or_1_out));
  ExactlyOne xor_2 (.out(out_4[1]), .in0(in_2[1]), .in1(in_3[1]), .in2(or_2_out));
  ExactlyOne xor_3 (.out(out_4[2]), .in0(in_2[2]), .in1(in_3[2]), .in2(or_3_out));
  ExactlyOne xor_4 (.out(out_4[3]), .in0(in_2[3]), .in1(in_3[3]), .in2(or_4_out));
  ExactlyOne xor_5 (.out(out_4[4]), .in0(in_2[4]), .in1(in_3[4]), .in2(or_5_out));
  ExactlyOne xor_6 (.out(out_4[5]), .in0(in_2[5]), .in1(in_3[5]), .in2(or_6_out));
  ExactlyOne xor_7 (.out(out_4[6]), .in0(in_2[6]), .in1(in_3[6]), .in2(or_7_out));
  ExactlyOne xor_8 (.out(out_4[7]), .in0(in_2[7]), .in1(in_3[7]), .in2(or_8_out));
  ExactlyOne xor_9 (.out(out_4[8]), .in0(in_2[8]), .in1(in_3[8]), .in2(or_9_out));
  ExactlyOne xor_10 (.out(out_4[9]), .in0(in_2[9]), .in1(in_3[9]), .in2(or_10_out));
  ExactlyOne xor_11 (.out(out_4[10]), .in0(in_2[10]), .in1(in_3[10]), .in2(or_11_out));
  ExactlyOne xor_12 (.out(out_4[11]), .in0(in_2[11]), .in1(in_3[11]), .in2(or_12_out));
  ExactlyOne xor_13 (.out(out_4[12]), .in0(in_2[12]), .in1(in_3[12]), .in2(or_13_out));
  ExactlyOne xor_14 (.out(out_4[13]), .in0(in_2[13]), .in1(in_3[13]), .in2(or_14_out));
  ExactlyOne xor_15 (.out(out_4[14]), .in0(in_2[14]), .in1(in_3[14]), .in2(or_15_out));
  ExactlyOne xor_16 (.out(out_4[15]), .in0(in_2[15]), .in1(in_3[15]), .in2(or_16_out));
endmodule
